# Fritzing sketch ldr_analog (saved by Fritzing 0.8.7b)
breadboards: 1

parts:
  e-radionica_com1 = LM393 LDR breakout [part_number=100027]
  Part1 = Arduino Uno (Rev3)

nets:
  VCC: e-radionica_com1.VCC, Part1.5V
  GND: e-radionica_com1.GND, Part1.GND
  N1: e-radionica_com1.AO, Part1.A0
